# Fritzing sketch watering (saved by Fritzing 0.9.3b)
breadboards: 1

parts:
  U1 = ESP8266 NodeMCU LoLin module
  Capacitive_Soil_Moisture_Sensor1 = DFRobot Capacitive Soil Moisture Sensor V1.0 [part_number=SEN0193]
  Part1 = Arduino Uno (Rev3)
  SM1 = 28BYJ-48 Stepper Motor [part_number=28BYJ-48]
  Driver1 = 28BYJ-48 Driver Module [part_number=ULN2003 package=THT]
  LED1 = LED - 5mm [color="Red (633nm)" package="5 mm [THT]"]
  M1 = Humidity and Temperature Sensor DHT11
  R1 = Resistor [tolerance=±5% resistance=220 package=THT]
  SG1 = Buzzer 12mm [part_number=COM-07950 package=buzzer-12mm-ns]

nets:
  N1: U1.D3, M1.Data
  N2: U1.D4, LED1.anode, R1.Pin_0, R1.Pin_1
  3V3: U1.3V3, M1.Vcc, SG1.2
  GND: U1.GND, LED1.cathode, M1.GND, SG1.1
  N3: U1.D5, Part1.D6_PWM
  N4: U1.D6, Part1.D5_PWM
  N5: Capacitive_Soil_Moisture_Sensor1.A, Part1.A0
  VCC: Capacitive_Soil_Moisture_Sensor1.VCC, Part1.3V3
  GND_2: Capacitive_Soil_Moisture_Sensor1.GND, Part1.GND, Driver1.GND
  N6: Part1.D8, Driver1.IN4
  N7: Part1.D9_PWM, Driver1.IN3
  N8: Part1.D10_PWM/SS, Driver1.IN2
  N9: Part1.D11_PWM/MOSI, Driver1.IN1
  N10: Part1.5V, Driver1.Vmotor
  N11: SM1.blue-pin, Driver1.blue-pin
  N12: SM1.pink-pin, Driver1.pink-pin
  N13: SM1.yellow-pin, Driver1.yellow-pin
  N14: SM1.orange-pin, Driver1.orange-pin
  N15: SM1.red-pin, Driver1.red-pin

custom parts:
  ESP8266 NodeMCU LoLin module: ESP8266 based NodeMCU
  DFRobot Capacitive Soil Moisture Sensor V1.0: DFRobot Capacitive Soil Moisture Sensor V1.0 This product measures soil moisture levels by capacitive sensing, rather than resistive sensing like other types of moisture sensor. It is made of a corrosion resistant material giving it a long service life. Insert it into soil and impress your friends with the real-time soil moisture data! The product includes an on-board voltage regulator which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
  28BYJ-48 Stepper Motor: Unipolar Stepper Motor 28BYJ-48 Top coil - pink & orange Bottom coil - blue & yellow Common rail - red Connector pins: blue - pink - yellow - orange - red
  28BYJ-48 Driver Module: High-power ULN2003 Stepper Motor Driver Board Test Module For Arduino AVR SMD
  Humidity and Temperature Sensor DHT11: Digital relative humidity & temperature sensor DHT11
  Buzzer 12mm: Buzzer 12mm Spark Fun Electronics SKU : Comp-Buzzer Through hole This is a small 12mm round speaker that operates around the audible 2kHz range. You can use these speakers to create simple music or user interfaces. This is not a true piezoelectric speaker but behaves similarly. Instead of a piezoelectric crystal that vibrates with an electric current, this tiny speaker uses an electromagnet to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
